# Fritzing sketch Circuit (saved by Fritzing 0.9.5d)
breadboards: 1

parts:
  Mod1 = TI Launchpad TM4C123GXL
  A1 = L298N DC motor driver
  JACK1 = 2.1mm Barrel Jack with Terminal Block
  M1 = Getriebemotor
  M2 = Getriebemotor
  S3 = D2F-FL Omron Snap Action Limit Switch with Level
  S4 = D2F-FL Omron Snap Action Limit Switch with Level
  S5 = Momentary Switch [package=ksa_sealed_tac_switch]
  R1 = Resistor [tolerance=±5% resistance=1k package="2010 [SMD]"]
  S8 = Toggle Switch [package=THT]
  R2 = Resistor [tolerance=±5% resistance=1k package="2010 [SMD]"]
  R3 = Resistor [tolerance=±5% resistance=1k package="2010 [SMD]"]
  S9 = Toggle Switch [package=THT]
  R4 = Resistor [tolerance=±5% resistance=1k package="2010 [SMD]"]
  R5 = Resistor [tolerance=±5% resistance=1k package="2010 [SMD]"]
  S10 = Toggle Switch [package=THT]
  R6 = Resistor [tolerance=±5% resistance=1k package="2010 [SMD]"]
  R7 = Resistor [tolerance=±5% resistance=1k package="2010 [SMD]"]
  S11 = D2F-FL Omron Snap Action Limit Switch with Level
  S12 = D2F-FL Omron Snap Action Limit Switch with Level
  S13 = Momentary Switch [package=ksa_sealed_tac_switch]
  R8 = Resistor [tolerance=±5% resistance=1k package="2010 [SMD]"]
  S14 = Momentary Switch [package=ksa_sealed_tac_switch]
  R9 = Resistor [tolerance=±5% resistance=1k package="2010 [SMD]"]

nets:
  N1: Mod1.PB0, S9.L1, R4.Pin_1
  N2: Mod1.PB1, S9.L2, R5.Pin_1
  N3: Mod1.PE4, S8.L1, R2.Pin_1
  N4: Mod1.PE5, S8.L2, R3.Pin_1
  N5: Mod1.PA5, S3.Pin_1
  N6: Mod1.PA6, S4.Pin_1
  N7: Mod1.PA7, S13.4, R8.Pin_1
  GND: Mod1.GND, A1.GND, JACK1.NEG, S3.Pin_2, S5.2, R2.Pin_0, R3.Pin_0, R4.Pin_0, R5.Pin_0, R6.Pin_0, R7.Pin_0, S11.Pin_2, S13.2
  N8: Mod1.PE2, S5.4, R1.Pin_1
  N9: Mod1.PE3, S14.4, R9.Pin_1
  N10: Mod1.PC6, S11.Pin_1
  N11: Mod1.PC7, S12.Pin_1
  N12: Mod1.PD6, S10.L1, R6.Pin_1
  N13: Mod1.PD7, S10.L2, R7.Pin_1
  N14: Mod1.PB6, A1.IN4
  N15: Mod1.PA4, A1.IN3
  N16: Mod1.PA3, A1.IN2
  N17: Mod1.PA2, A1.IN1
  N18: A1.OUT1, M1.pin_1
  N19: A1.12V, JACK1.POS
  N20: A1.5V, A1.+5V-J1, A1.+5V-J2, A1.ENA, A1.ENB, S3.Pin_3, R1.Pin_0, S8.COM, S9.COM, S11.Pin_3, R8.Pin_0, R9.Pin_0
  N21: A1.OUT3, M2.pin_1

notes:
  Driver-to-Passenger Window Control Switch
  Driver Window Control Switch
  Passenger Window Control Switch

custom parts:
  L298N DC motor driver: This L298N Motor Driver Module is a high power motor driver module for driving DC and Stepper Motors. This module consists of an L298 motor driver IC and a 78M05 5V regulator.
  D2F-FL Omron Snap Action Limit Switch with Level: Snap action switch with stainless steel lever.
